# Fritzing sketch _03_aModaDoPiscaPisca_EX1 (saved by Fritzing 0.9.3b)
breadboards: 1

parts:
  R1 = Resistor [tolerance=±5% resistance=220 package=THT]
  LED1 = LED - 5mm [color="Red (633nm)" package="5 mm [THT]"]
  Part1 = Arduino Uno (Rev3)
  LED2 = LED - 5mm [color="Orange (605nm)" package="5 mm [THT]"]
  LED3 = LED - 5mm [color="Green (560nm)" package="5 mm [THT]"]
  R2 = Resistor [tolerance=±5% resistance=220 package=THT]
  R3 = Resistor [tolerance=±5% resistance=220 package=THT]

nets:
  N1: R1.Pin_0, Part1.GND, R2.Pin_0, R3.Pin_0
  N2: R1.Pin_1, LED1.cathode
  N3: Part1.D8, LED3.anode
  N4: Part1.D9_PWM, LED2.anode
  N5: LED2.cathode, R2.Pin_1
  N6: LED3.cathode, R3.Pin_1
