# Fritzing sketch _04_ComandoNaMaoECarregaNoBotao_simples (saved by Fritzing 0.9.3b)
breadboards: 1

parts:
  R1 = Resistor [tolerance=±5% resistance=220 package=THT]
  LED1 = LED - 5mm [color="Red (633nm)" package="5 mm [THT]"]
  Part1 = Arduino Uno (Rev3)
  S1 = Pushbutton [package="[THT]"]
  R4 = Resistor [tolerance=±5% resistance=10k package=THT]

nets:
  N1: R1.Pin_0, Part1.GND, R4.Pin_0
  N2: R1.Pin_1, LED1.cathode
  N3: LED1.anode, Part1.D10_PWM/SS
  N4: Part1.D7, S1.Pin_3, S1.Pin_4, R4.Pin_1
  N5: Part1.5V, S1.Pin_1, S1.Pin_2
